# Fritzing sketch senzor_gaze_proiect_final (saved by Fritzing 0.9.5d)
breadboards: 1

parts:
  Part1 = Arduino Uno (Rev3)
  LED1 = smd LED [color="Red (633nm)" package="0603 [SMD]"]
  LED2 = smd LED [color="Green (555nm)" package="0603 [SMD]"]
  Buzzer = Piezo Speaker
  MQ-2_senzor_gaz = GAS_SENSOR [package=mq-3]
  R1 = Resistor [tolerance=±5% resistance=220 package=THT]
  R2 = Resistor [tolerance=±5% resistance=220 package=THT]
  R3 = Resistor [tolerance=±5% resistance=220 package=THT]

nets:
  N1: Part1.D10_PWM/SS, Buzzer.pin2
  N2: Part1.D11_PWM/MOSI, LED2.anode
  N3: Part1.D12/MISO, LED1.anode
  N4: Part1.GND, MQ-2_senzor_gaz.A1, R1.Pin_1, R2.Pin_1, R3.Pin_1
  N5: Part1.5V, MQ-2_senzor_gaz.B1
  N6: LED1.cathode, R1.Pin_0
  N7: LED2.cathode, R2.Pin_0
  N8: Buzzer.pin1, R3.Pin_0
  N9: MQ-2_senzor_gaz.H1, MQ-2_senzor_gaz.H2
